# Fritzing sketch carteMere (saved by Fritzing 0.9.3b)
circuit board: 4.8cm x 5.64444cm
breadboards: 1

parts:
  HC-05 = Bluetooth HC05 SMD [package=SMD]
  JP1 = Header 6 [package=molex-1x6-ra_lock]
  Arduino_PM_3v3 = Arduino Pro Mini (3.3V)
  TP4056 = SO08 [chip_label=IC package=SO]
  Btn1 = Adafruit Push-button Power Switch Breakout [package=THT]
  AL = Header 2 [package=jst-2-pth-ns]
  JP3 = Header 1 [package=1x01_offset]
  JP4 = Header 1 [package=1x01_offset]
  R1 = Resistor [tolerance=±5% resistance=47 package="1206 [SMD]"]
  R2 = Resistor [tolerance=±5% resistance=47 package="1206 [SMD]"]
  Rprog = Resistor [tolerance=±5% resistance=1.5k package="1206 [SMD]"]
  C1 = Capacitor [package=0805]
  STD = Header 2 [package=molex-1x2_lock]
  CHG = Header 2 [package=molex-1x2_lock]
  C2 = Capacitor [package=0805]
  BAT = Header 2 [package=jst-2-pth-ns]

nets:
  N1: HC-05.pin1, Arduino_PM_3v3.MOSI
  N2: HC-05.pin3, Arduino_PM_3v3.D10
  N3: HC-05.pin12, JP1.5, Arduino_PM_3v3.VCC
  GND: HC-05.pin13, HC-05.pin21, JP1.6, Arduino_PM_3v3.GND, TP4056.TEMP, TP4056.GND, Btn1.GND, AL.1, Rprog.Pin_0, C1.1, C2.2, BAT.1
  N4: JP1.1, Arduino_PM_3v3.D5
  N5: JP1.2, Arduino_PM_3v3.D4
  N6: JP1.3, Arduino_PM_3v3.D3
  N7: JP1.4, Arduino_PM_3v3.D2
  N8: Arduino_PM_3v3.RAW, Btn1.OUT
  N9: Arduino_PM_3v3.SCK, JP4.1
  N10: TP4056.PROG, Rprog.Pin_1
  N11: TP4056.VCC, TP4056.CE, AL.2, C1.2, STD.2, CHG.2
  N12: TP4056.BAT, Btn1.IN, C2.1, BAT.2
  N13: TP4056.STDBY, R1.Pin_0
  N14: TP4056.CHRG, R2.Pin_0
  N15: Btn1.OFF, JP3.1
  N16: R1.Pin_1, STD.1
  N17: R2.Pin_1, CHG.1

custom parts:
  Bluetooth HC05 SMD: Serial port Bluetooth module (Master/Slave) HC05 bare SMD board.
