# Fritzing sketch feuPWM (saved by Fritzing 0.9.3b)
circuit board: 8.46667cm x 3cm
breadboards: 1

parts:
  U1 = 74HC595 SMD [package="SO16 [SMD]"]
  RGB_SMD_LED1 = SMD RGB LED (WS2812) [package=5050]
  R1 = Resistor [tolerance=±5% resistance=220 package="0805 [SMD]"]
  RGB_SMD_LED2 = SMD RGB LED (WS2812) [package=5050]
  R2 = Resistor [tolerance=±5% resistance=220 package="0805 [SMD]"]
  RGB_SMD_LED3 = SMD RGB LED (WS2812) [package=5050]
  R3 = Resistor [tolerance=±5% resistance=220 package="0805 [SMD]"]
  RGB_SMD_LED4 = SMD RGB LED (WS2812) [package=5050]
  R4 = Resistor [tolerance=±5% resistance=220 package="0805 [SMD]"]
  RGB_SMD_LED5 = SMD RGB LED (WS2812) [package=5050]
  R5 = Resistor [tolerance=±5% resistance=220 package="0805 [SMD]"]
  RGB_SMD_LED6 = SMD RGB LED (WS2812) [package=5050]
  R6 = Resistor [tolerance=±5% resistance=220 package="0805 [SMD]"]
  RGB_SMD_LED7 = SMD RGB LED (WS2812) [package=5050]
  R7 = Resistor [tolerance=±5% resistance=220 package="0805 [SMD]"]
  RGB_SMD_LED8 = SMD RGB LED (WS2812) [package=5050]
  R8 = Resistor [tolerance=±5% resistance=220 package="0805 [SMD]"]
  JP7 = Header 4 [package=jst-4-pth]
  JP1 = Header 6 [package=molex-1x6-ra_lock]
  JP2 = Header 6 [package=molex-1x6-ra_lock]
  Q2 = PNP-Transistor [package="SOT-23 [SMD]"]
  R9 = Resistor [tolerance=±5% resistance=220 package="0805 [SMD]"]
  R10 = Resistor [tolerance=±5% resistance=220 package="0805 [SMD]"]
  Q1 = NPN-Transistor [package="SOT-23 [SMD]"]
  JP8 = Header 4 [package=jst-4-pth]
  JP10 = Header 1 [package=1x01_offset]
  JP11 = Header 1 [package=1x01_offset]

nets:
  N1: U1.Q1, R2.Pin_0
  N2: U1.Q2, R3.Pin_0
  N3: U1.Q3, R4.Pin_0
  N4: U1.Q4, R5.Pin_0
  N5: U1.Q5, R6.Pin_0
  N6: U1.Q6, R7.Pin_0
  N7: U1.Q7, R8.Pin_0
  N8: U1.GND, U1.OE, JP1.1, Q2.2, Q1.2, JP11.1
  N9: U1.Q7', JP8.1
  N10: U1.MR, JP1.2, JP8.2
  N11: U1.SH_CP, JP1.3, JP8.3
  N12: U1.ST_CP, JP1.4, JP8.4
  N13: U1.DS, JP1.5
  N14: U1.Q0, R1.Pin_0
  N15: U1.VCC, JP7.4, JP2.5
  N16: RGB_SMD_LED1.DOut, RGB_SMD_LED1.DIn, RGB_SMD_LED1.VCC, R1.Pin_1
  VDD: RGB_SMD_LED1.NC, RGB_SMD_LED1.VDD, RGB_SMD_LED1.VSS, RGB_SMD_LED2.NC, RGB_SMD_LED2.VDD, RGB_SMD_LED2.VSS, RGB_SMD_LED3.NC, RGB_SMD_LED3.VDD, RGB_SMD_LED3.VSS, RGB_SMD_LED4.NC, RGB_SMD_LED4.VDD, RGB_SMD_LED4.VSS, Q1.1
  N17: RGB_SMD_LED2.DOut, RGB_SMD_LED2.DIn, RGB_SMD_LED2.VCC, R2.Pin_1
  N18: RGB_SMD_LED3.DOut, RGB_SMD_LED3.DIn, RGB_SMD_LED3.VCC, R3.Pin_1
  N19: RGB_SMD_LED4.DOut, RGB_SMD_LED4.DIn, RGB_SMD_LED4.VCC, R4.Pin_1
  N20: RGB_SMD_LED5.DOut, RGB_SMD_LED5.DIn, RGB_SMD_LED5.VCC, R5.Pin_1
  VDD_2: RGB_SMD_LED5.NC, RGB_SMD_LED5.VDD, RGB_SMD_LED5.VSS, RGB_SMD_LED6.NC, RGB_SMD_LED6.VDD, RGB_SMD_LED6.VSS, RGB_SMD_LED7.NC, RGB_SMD_LED7.VDD, RGB_SMD_LED7.VSS, RGB_SMD_LED8.NC, RGB_SMD_LED8.VDD, RGB_SMD_LED8.VSS, Q2.1
  N21: RGB_SMD_LED6.DOut, RGB_SMD_LED6.DIn, RGB_SMD_LED6.VCC, R6.Pin_1
  N22: RGB_SMD_LED7.DOut, RGB_SMD_LED7.DIn, RGB_SMD_LED7.VCC, R7.Pin_1
  N23: RGB_SMD_LED8.DOut, RGB_SMD_LED8.DIn, RGB_SMD_LED8.VCC, R8.Pin_1
  N24: JP7.1, JP2.2
  N25: JP7.2, JP2.3
  N26: JP7.3, JP2.4
  N27: JP1.6, JP2.1, R9.Pin_1, R10.Pin_1
  N28: JP2.6, JP10.1
  N29: Q2.0, R9.Pin_0
  N30: R10.Pin_0, Q1.0
